// Logisim project part2.circ as structural Verilog: 3 circuits, main circuit encoder
module main (
  input  Car_0,
  input  Car_1,
  input  Car_2,
  input  Car_3,
  input  Car_4,
  input  Car_5,
  input  Car_6,
  input  Car_7,
  input  Car_8,
  input  Car_9
);

  encoder encoder_1 (
    .i0(Car_0), .i1(Car_1), .i2(Car_2), .i3(Car_3), .i4(Car_4), .i5(Car_5), .i6(Car_6), .i7(Car_7),
    .i8(Car_8), .i9(Car_9));  // open: o0, o1, o2, o3
  _7_Segment_Display #(.decimalPoint("false")) u_7_segment_display_1 ();  // open: g, f, a, b, e, d, c
endmodule

module encoder (
  input  i0,
  input  i1,
  input  i2,
  input  i3,
  input  i4,
  input  i5,
  input  i6,
  input  i7,
  input  i8,
  input  i9,
  output o0,
  output o1,
  output o2,
  output o3
);

  wire n7432_1_pin3, n7432_1_pin6, n7432_1_pin11, n7432_2_pin3, n7432_2_pin6, n7432_2_pin11, n7432_3_pin3,
       n7432_3_pin11, n7432_4_pin3;

  _7432 #(.ShowInternalStructure("true")) u_7432_1 (
    .pin1(i4), .pin2(i2), .pin3(n7432_1_pin3), .pin4(n7432_1_pin3), .pin5(i0), .pin6(n7432_1_pin6),
    .pin13(i6), .pin12(i8), .pin11(n7432_1_pin11), .pin10(n7432_1_pin11), .pin9(n7432_1_pin6), .pin8(o0));
  _7432 #(.ShowInternalStructure("true")) u_7432_2 (
    .pin1(i5), .pin2(i2), .pin3(n7432_2_pin3), .pin4(n7432_2_pin3), .pin5(i1), .pin6(n7432_2_pin6),
    .pin13(i6), .pin12(i9), .pin11(n7432_2_pin11), .pin10(n7432_2_pin11), .pin9(n7432_2_pin6), .pin8(o1));
  _7432 #(.ShowInternalStructure("true")) u_7432_3 (
    .pin1(i4), .pin2(i3), .pin3(n7432_3_pin3), .pin13(i5), .pin12(i6), .pin11(n7432_3_pin11),
    .pin10(n7432_3_pin11), .pin9(n7432_3_pin3), .pin8(o2));  // open: pin4, pin5, pin6
  _7432 #(.ShowInternalStructure("true")) u_7432_4 (
    .pin1(i7), .pin2(i8), .pin3(n7432_4_pin3), .pin4(n7432_4_pin3), .pin5(i9), .pin6(o3));  // open: pin13, pin12, pin11, pin10, pin9, pin8
endmodule

module dec0der (
  input  i0,
  input  i1,
  input  i2,
  input  i3,
  output o0,
  output o1,
  output o2,
  output o3,
  output o4,
  output o5,
  output o6
);
endmodule
