// Logisim project problem3.circ as structural Verilog: 1 circuit, main circuit main
module main (
  input  in_1,
  input  [3:0] in_2
);

  Clock clock_1 ();  // open: out
  Decoder #(.select(3)) decoder_1 ();  // open: out0, out1, out2, out3, out4, out5, out6, out7, sel, en
endmodule
