// Logisim project cpu.circ as structural Verilog
module fetch (
);

  instruction_memory instruction_memory_1 ();  // open: PC, clk, byte_0, byte_1, byte_2, byte_3, byte_4, byte_5, byte_6, byte_7, byte_8, byte_9
endmodule

module instruction_memory (
  input  [63:0] PC,
  input  clk,
  output [7:0] byte_0,
  output [7:0] byte_1,
  output [7:0] byte_2,
  output [7:0] byte_3,
  output [7:0] byte_4,
  output [7:0] byte_5,
  output [7:0] byte_6,
  output [7:0] byte_7,
  output [7:0] byte_8,
  output [7:0] byte_9
);

  wire and_8_out, d_ff_1_q, d_ff_1_qn, decoder_1_out0, decoder_1_out1, decoder_1_out2, decoder_1_out3,
       decoder_1_out4, decoder_1_out5, decoder_1_out6, decoder_1_out7, decoder_1_out8, decoder_1_out9,
       or_1_out, or_3_out;
  wire [3:0] adder_1_out, and_1_out, and_2_out, and_3_out, and_4_out, and_5_out, and_6_out, and_7_out,
       or_2_out, register_2_q;
  wire [7:0] ram_1_dout;
  wire [11:0] register_1_q;

  Register #(.width(12)) register_1 (.D(PC[11:0]), .clk(clk), .Q(register_1_q));  // open: en, clr
  D_Flip_Flop d_ff_1 (.D(or_1_out), .clk(clk), .Q(d_ff_1_q), .Qn(d_ff_1_qn));  // open: preset, reset
  assign and_1_out = byte_0[7:4] & 4'b0010;  // AND_Gate and_1, 4 bits wide
  assign and_2_out = byte_0[7:4] & 4'b0011;  // AND_Gate and_2, 4 bits wide
  assign and_3_out = byte_0[7:4] & 4'b0100;  // AND_Gate and_3, 4 bits wide
  assign and_4_out = byte_0[7:4] & 4'b0101;  // AND_Gate and_4, 4 bits wide
  assign and_5_out = byte_0[7:4] & 4'b0110;  // AND_Gate and_5, 4 bits wide
  assign and_6_out = byte_0[7:4] & 4'b1010;  // AND_Gate and_6, 4 bits wide
  assign and_7_out = byte_0[7:4] & 4'b1011;  // AND_Gate and_7, 4 bits wide
  RAM #(.addrWidth(12)) ram_1 (.addr(register_1_q), .dout(ram_1_dout));  // open: we, oe, clk, din
  Register #(.width(4)) register_2 (.D(adder_1_out), .en(d_ff_1_q), .clk(clk), .Q(register_2_q));  // open: clr
  or or_1 (or_1_out, d_ff_1_q, d_ff_1_qn);
  assign or_2_out = and_1_out | and_2_out | and_3_out | and_4_out | and_5_out | and_6_out | and_7_out;  // OR_Gate or_2, 4 bits wide
  or or_3 (or_3_out, or_2_out[0], or_2_out[1], or_2_out[2], or_2_out[3]);
  Adder #(.width(4)) adder_1 (.a(register_2_q), .b(4'b0001), .out(adder_1_out));  // open: cin, cout
  Decoder #(.select(4)) decoder_1 (
    .out0(decoder_1_out0), .out1(decoder_1_out1), .out2(decoder_1_out2), .out3(decoder_1_out3),
    .out4(decoder_1_out4), .out5(decoder_1_out5), .out6(decoder_1_out6), .out7(decoder_1_out7),
    .out8(decoder_1_out8), .out9(decoder_1_out9), .sel(register_2_q));  // open: out10, out11, out12, out13, out14, out15, en
  and and_8 (and_8_out, or_3_out, decoder_1_out1);
  assign byte_0 = decoder_1_out0 ? ram_1_dout : 8'bz;  // Controlled_Buffer controlled_buffer_1
  assign byte_1 = and_8_out ? ram_1_dout : 8'bz;  // Controlled_Buffer controlled_buffer_2
  assign byte_2 = decoder_1_out2 ? ram_1_dout : 8'bz;  // Controlled_Buffer controlled_buffer_3
  assign byte_3 = decoder_1_out3 ? ram_1_dout : 8'bz;  // Controlled_Buffer controlled_buffer_4
  assign byte_4 = decoder_1_out4 ? ram_1_dout : 8'bz;  // Controlled_Buffer controlled_buffer_5
  assign byte_5 = decoder_1_out5 ? ram_1_dout : 8'bz;  // Controlled_Buffer controlled_buffer_6
  assign byte_6 = decoder_1_out6 ? ram_1_dout : 8'bz;  // Controlled_Buffer controlled_buffer_7
  assign byte_7 = decoder_1_out7 ? ram_1_dout : 8'bz;  // Controlled_Buffer controlled_buffer_8
  assign byte_8 = decoder_1_out8 ? ram_1_dout : 8'bz;  // Controlled_Buffer controlled_buffer_9
  assign byte_9 = decoder_1_out9 ? ram_1_dout : 8'bz;  // Controlled_Buffer controlled_buffer_10

  // Notes on the sheet:
  //   this line increments pc by 1 byte
endmodule
